// Logisim project alu32bits.circ as structural Verilog: 1 circuit, main circuit main
module main (
  input  [31:0] in_1,
  input  [31:0] in_2,
  input  [30:0] in_3,
  input  [3:0] in_4,
  output [31:0] out_5
);

  wire [0:0] comparator_1_eq, comparator_1_gt, comparator_1_lt;
  wire [31:0] adder_1_out, and_1_out, divider_1_out, multiplier_1_out, or_1_out, shifter_1_out,
       subtractor_1_out, xor_1_out;

  Adder #(.width(32)) adder_1 (.a(in_1), .b(in_2), .out(adder_1_out));  // open: cin, cout
  Subtractor #(.width(32)) subtractor_1 (.a(in_1), .b(in_2), .out(subtractor_1_out));  // open: bin, bout
  Multiplier #(.width(32)) multiplier_1 (.a(in_1), .b(in_2), .out(multiplier_1_out));  // open: cin, cout
  Divider #(.width(32)) divider_1 (.a(in_1), .b(in_2), .out(divider_1_out));  // open: upper, rem
  Multiplexer #(.select(4), .width(32), .enable("false")) multiplexer_1 (
    .in0(adder_1_out), .in1(subtractor_1_out), .in2(multiplier_1_out), .in3(divider_1_out), .in4(and_1_out),
    .in5(or_1_out), .in6(xor_1_out), .in7(shifter_1_out), .in8({in_3, comparator_1_lt[0]}),
    .in9({in_3, comparator_1_eq[0]}), .in10({in_3, comparator_1_gt[0]}), .out(out_5), .sel(in_4));  // open: in11, in12, in13, in14, in15
  assign and_1_out = in_1 & in_2;  // AND_Gate and_1, 32 bits wide
  assign or_1_out = in_1 | in_2;  // OR_Gate or_1, 32 bits wide
  assign xor_1_out = in_1 ^ in_2;  // XOR_Gate xor_1, 32 bits wide
  Shifter #(.width(32), .shift("lr")) shifter_1 (.in(in_1), .\dist (in_2[4:0]), .out(shifter_1_out));
  Comparator #(.width(32)) comparator_1 (
    .a(in_1), .b(in_2), .gt(comparator_1_gt[0]), .eq(comparator_1_eq[0]), .lt(comparator_1_lt[0]));
endmodule
