// Logisim project adder8bits.circ as structural Verilog: 1 circuit, main circuit main
module main (
  input  in_1,
  input  [7:0] in_2,
  input  [7:0] in_3,
  output [7:0] out_4,
  output out_5
);

  wire adder_1_cout, adder_2_cout, adder_3_cout, adder_4_cout, adder_5_cout, adder_6_cout, adder_7_cout;

  Adder #(.width(1)) adder_1 (.a(in_2[0]), .b(in_3[0]), .out(out_4[0]), .cin(in_1), .cout(adder_1_cout));
  Adder #(.width(1)) adder_2 (.a(in_2[1]), .b(in_3[1]), .out(out_4[1]), .cin(adder_1_cout), .cout(adder_2_cout));
  Adder #(.width(1)) adder_3 (.a(in_2[2]), .b(in_3[2]), .out(out_4[2]), .cin(adder_2_cout), .cout(adder_3_cout));
  Adder #(.width(1)) adder_4 (.a(in_2[3]), .b(in_3[3]), .out(out_4[3]), .cin(adder_3_cout), .cout(adder_4_cout));
  Adder #(.width(1)) adder_5 (.a(in_2[4]), .b(in_3[4]), .out(out_4[4]), .cin(adder_4_cout), .cout(adder_5_cout));
  Adder #(.width(1)) adder_6 (.a(in_2[5]), .b(in_3[5]), .out(out_4[5]), .cin(adder_5_cout), .cout(adder_6_cout));
  Adder #(.width(1)) adder_7 (.a(in_2[6]), .b(in_3[6]), .out(out_4[6]), .cin(adder_6_cout), .cout(adder_7_cout));
  Adder #(.width(1)) adder_8 (.a(in_3[7]), .b(in_2[7]), .out(out_4[7]), .cin(adder_7_cout), .cout(out_5));
endmodule
