// Logisim project counter.circ as structural Verilog: 1 circuit, main circuit main
module main (
  input  R,
  output [4:0] out_2
);

  wire clock_1_out;
  wire [4:0] adder_1_out, multiplexer_1_out;

  Multiplexer #(.width(5), .enable("false")) multiplexer_1 (
    .in0(adder_1_out), .in1({5{1'b0}}), .out(multiplexer_1_out), .sel(R));
  Clock clock_1 (.out(clock_1_out));
  Register #(.width(5)) register_1 (.D(multiplexer_1_out), .Q(out_2), .clk(clock_1_out));  // open: en, clr
  Adder #(.width(5)) adder_1 (.a(out_2), .b(5'b00001), .out(adder_1_out));  // open: cin, cout
endmodule
