// Logisim project decoder8bits.circ as structural Verilog: 1 circuit, main circuit main
module main (
  input  s2,
  input  s1,
  input  s1_2,
  output z0,
  output z1,
  output z2,
  output z3,
  output z4,
  output z5,
  output z6,
  output z7
);

  wire not_1_out, not_2_out, not_3_out;

  not not_1 (not_1_out, s2);
  not not_2 (not_2_out, s1);
  not not_3 (not_3_out, s1_2);
  and and_1 (z0, not_1_out, not_2_out, not_3_out);
  and and_2 (z1, not_1_out, not_2_out, s1_2);
  and and_3 (z2, not_1_out, s1, not_3_out);
  and and_4 (z3, not_1_out, s1, s1_2);
  and and_5 (z4, s2, not_2_out, not_3_out);
  and and_6 (z5, s2, not_2_out, s1_2);
  and and_7 (z6, s2, s1, not_3_out);
  and and_8 (z7, s2, s1, s1_2);
endmodule
