// Logisim project hexadecimalDisplay.circ as structural Verilog: 1 circuit, main circuit main
module main (
  input  [7:0] in_1
);

  wire [7:0] rom_1_data, rom_2_data;

  ROM #(.addrWidth(4)) rom_1 (.addr(in_1[7:4]), .data(rom_1_data));  // open: sel
  ROM #(.addrWidth(4)) rom_2 (.addr(in_1[3:0]), .data(rom_2_data));  // open: sel
  _7_Segment_Display u_7_segment_display_1 (
    .g(rom_1_data[3]), .f(rom_1_data[2]), .a(rom_1_data[1]), .b(rom_1_data[0]), .e(rom_1_data[7]),
    .d(rom_1_data[6]), .c(rom_1_data[5]), .dp(rom_1_data[4]));
  _7_Segment_Display u_7_segment_display_2 (
    .g(rom_2_data[3]), .f(rom_2_data[2]), .a(rom_2_data[1]), .b(rom_2_data[0]), .e(rom_2_data[7]),
    .d(rom_2_data[6]), .c(rom_2_data[5]), .dp(rom_2_data[4]));

  // Notes on the sheet:
  //   contents of rom_1 (hex, n*v repeats v):
  //   e7 21 cb 6b 2d 6e ee 23 ef 6f af ec c6 e9 ce 8e
  //   contents of rom_2 (hex, n*v repeats v):
  //   e7 21 cb 6b 2d 6e ee 23 ef 6f af ec c6 e9 ce 8e
endmodule
