// Logisim project multiplexer8inputBits.circ as structural Verilog: 1 circuit, main circuit main
module main (
  input  x0,
  input  x1,
  input  x2,
  input  x3,
  input  x4,
  input  x5,
  input  x6,
  input  x7,
  input  s2,
  input  s1,
  input  s0,
  output out_12
);

  wire and_1_out, and_2_out, and_3_out, and_4_out, and_5_out, and_6_out, and_7_out, and_8_out, not_1_out,
       not_2_out, not_3_out;

  not not_1 (not_1_out, s2);
  not not_2 (not_2_out, s1);
  not not_3 (not_3_out, s0);
  and and_1 (and_1_out, x0, not_1_out, not_2_out, not_3_out);
  and and_2 (and_2_out, x1, not_1_out, not_2_out, s0);
  and and_3 (and_3_out, x2, not_1_out, s1, not_3_out);
  and and_4 (and_4_out, x3, not_1_out, s1, s0);
  and and_5 (and_5_out, x4, s2, not_2_out, not_3_out);
  and and_6 (and_6_out, x5, s2, not_2_out, s0);
  and and_7 (and_7_out, x6, s2, s1, not_3_out);
  and and_8 (and_8_out, x7, s2, s1, s0);
  or or_1 (out_12, and_1_out, and_2_out, and_3_out, and_4_out, and_5_out, and_6_out, and_7_out, and_8_out);
endmodule
