// Logisim project rsLatch.circ as structural Verilog: 1 circuit, main circuit main
module main (
  input  S,
  input  R,
  output Q
);

  wire nor_1_out;

  nor nor_1 (nor_1_out, S, Q);
  nor nor_2 (Q, nor_1_out, R);
endmodule
