// Logisim project trafficLight.circ as structural Verilog: 1 circuit, main circuit main
module main (
  input  R,
  input  in_2,
  output [4:0] out_3
);

  wire and_1_out, and_2_out, and_3_out, and_4_out, clock_1_out, comparator_1_eq, comparator_1_lt,
       comparator_2_eq, comparator_2_gt, comparator_2_lt, comparator_3_eq, comparator_3_gt, comparator_3_lt,
       decoder_1_out0, decoder_1_out1, or_1_out, or_2_out, or_3_out, or_4_out, or_5_out;
  wire [4:0] adder_1_out, multiplexer_1_out;

  Multiplexer #(.width(5), .enable("false")) multiplexer_1 (
    .in0(adder_1_out), .in1({5{1'b0}}), .out(multiplexer_1_out), .sel(or_1_out));
  or or_1 (or_1_out, comparator_1_eq, decoder_1_out1, R);
  Clock clock_1 (.out(clock_1_out));
  Decoder #(.enable("false")) decoder_1 (.out0(decoder_1_out0), .out1(decoder_1_out1), .sel(in_2));
  Register #(.width(5)) register_1 (.D(multiplexer_1_out), .Q(out_3), .clk(clock_1_out));  // open: en, clr
  Adder #(.width(5)) adder_1 (.a(out_3), .b(5'b00001), .out(adder_1_out));  // open: cin, cout
  Comparator #(.width(5), .mode("unsigned")) comparator_1 (
    .a(out_3), .b({5{1'b1}}), .eq(comparator_1_eq), .lt(comparator_1_lt));  // open: gt
  Comparator #(.width(5), .mode("unsigned")) comparator_2 (
    .a(out_3), .b(5'b10011), .gt(comparator_2_gt), .eq(comparator_2_eq), .lt(comparator_2_lt));
  Comparator #(.width(5), .mode("unsigned")) comparator_3 (
    .a(out_3), .b(5'b01101), .gt(comparator_3_gt), .eq(comparator_3_eq), .lt(comparator_3_lt));
  or or_2 (or_2_out, comparator_1_eq, comparator_1_lt);
  or or_3 (or_3_out, comparator_2_eq, comparator_2_lt);
  or or_4 (or_4_out, comparator_3_eq, comparator_3_lt);
  and and_1 (and_1_out, or_2_out, decoder_1_out0, comparator_2_gt);
  and and_2 (and_2_out, or_3_out, decoder_1_out0, comparator_3_gt);
  and and_3 (and_3_out, decoder_1_out0, or_4_out);
  and and_4 (and_4_out, decoder_1_out1, clock_1_out);
  LED led_1 (.in(and_1_out));
  LED led_2 (.in(or_5_out));
  or or_5 (or_5_out, and_2_out, and_4_out);
  LED led_3 (.in(and_3_out));
endmodule
